// Logisim project alu.circ as structural Verilog
module _8bit_AND (
  input  [7:0] A,
  input  [7:0] B,
  output [7:0] Output
);

  and and_1 (Output[0], A[0], B[0]);
  and and_2 (Output[1], A[1], B[1]);
  and and_3 (Output[2], A[2], B[2]);
  and and_4 (Output[3], A[3], B[3]);
  and and_5 (Output[4], A[4], B[4]);
  and and_6 (Output[5], A[5], B[5]);
  and and_7 (Output[6], A[6], B[6]);
  and and_8 (Output[7], A[7], B[7]);
endmodule

module _8bit_OR (
  input  [7:0] A,
  input  [7:0] B,
  output [7:0] Output
);

  or or_1 (Output[0], A[0], B[0]);
  or or_2 (Output[1], A[1], B[1]);
  or or_3 (Output[2], A[2], B[2]);
  or or_4 (Output[3], A[3], B[3]);
  or or_5 (Output[4], A[4], B[4]);
  or or_6 (Output[5], A[5], B[5]);
  or or_7 (Output[6], A[6], B[6]);
  or or_8 (Output[7], A[7], B[7]);
endmodule

module _8bit_XOR (
  input  [7:0] A,
  input  [7:0] B,
  output [7:0] Output
);

  xor xor_1 (Output[0], A[0], B[0]);
  xor xor_2 (Output[1], A[1], B[1]);
  xor xor_3 (Output[2], A[2], B[2]);
  xor xor_4 (Output[3], A[3], B[3]);
  xor xor_5 (Output[4], A[4], B[4]);
  xor xor_6 (Output[5], A[5], B[5]);
  xor xor_7 (Output[6], A[6], B[6]);
  xor xor_8 (Output[7], A[7], B[7]);
endmodule

module _8bit_add_sub (
  input  Control,
  input  [7:0] A,
  input  [7:0] B,
  output [7:0] Output
);

  wire adder_1_cout, adder_2_cout, adder_3_cout, adder_4_cout, adder_5_cout, adder_6_cout, adder_7_cout,
       xor_1_out, xor_2_out, xor_3_out, xor_4_out, xor_5_out, xor_6_out, xor_7_out, xor_8_out;

  xor xor_1 (xor_1_out, Control, B[0]);
  xor xor_2 (xor_2_out, Control, B[1]);
  xor xor_3 (xor_3_out, Control, B[2]);
  xor xor_4 (xor_4_out, Control, B[3]);
  xor xor_5 (xor_5_out, Control, B[4]);
  xor xor_6 (xor_6_out, Control, B[5]);
  xor xor_7 (xor_7_out, Control, B[6]);
  xor xor_8 (xor_8_out, Control, B[7]);
  Adder #(.width(1)) adder_1 (.a(A[0]), .b(xor_1_out), .out(Output[0]), .cin(Control), .cout(adder_1_cout));
  Adder #(.width(1)) adder_2 (.a(A[1]), .b(xor_2_out), .out(Output[1]), .cin(adder_1_cout), .cout(adder_2_cout));
  Adder #(.width(1)) adder_3 (.a(A[2]), .b(xor_3_out), .out(Output[2]), .cin(adder_2_cout), .cout(adder_3_cout));
  Adder #(.width(1)) adder_4 (.a(A[3]), .b(xor_4_out), .out(Output[3]), .cin(adder_3_cout), .cout(adder_4_cout));
  Adder #(.width(1)) adder_5 (.a(A[4]), .b(xor_5_out), .out(Output[4]), .cin(adder_4_cout), .cout(adder_5_cout));
  Adder #(.width(1)) adder_6 (.a(A[5]), .b(xor_6_out), .out(Output[5]), .cin(adder_5_cout), .cout(adder_6_cout));
  Adder #(.width(1)) adder_7 (.a(A[6]), .b(xor_7_out), .out(Output[6]), .cin(adder_6_cout), .cout(adder_7_cout));
  Adder #(.width(1)) adder_8 (.a(A[7]), .b(xor_8_out), .out(Output[7]), .cin(adder_7_cout));  // open: cout

  // Notes on the sheet:
  //   0 = add; 1 = sub
endmodule

module _2bit_mul (
  input  A0,
  input  A1,
  input  B0,
  input  B1,
  output R0,
  output R1,
  output R2,
  output R3
);

  wire and_1_out, and_3_out, and_4_out, and_5_out;

  and and_1 (and_1_out, A0, B1);
  and and_2 (R0, A0, B0);
  and and_3 (and_3_out, A1, B0);
  and and_4 (and_4_out, A1, B1);
  and and_5 (and_5_out, and_1_out, and_3_out);
  xor xor_1 (R1, and_1_out, and_3_out);
  xor xor_2 (R2, and_5_out, and_4_out);
  and and_6 (R3, and_5_out, and_4_out);
endmodule

module _1bit_alu (
  input  Cin,
  input  [1:0] Operation,
  input  A,
  input  B,
  input  add_sub,
  output out_6,
  output Cout
);

  wire adder_1_out, and_1_out, multiplexer_1_out, not_1_out, or_1_out, xor_1_out;

  not not_1 (not_1_out, B);
  Multiplexer #(.enable("false")) multiplexer_1 (.in0(B), .in1(not_1_out), .out(multiplexer_1_out), .sel(add_sub));
  and and_1 (and_1_out, A, B);
  or or_1 (or_1_out, A, B);
  xor xor_1 (xor_1_out, A, B);
  Adder #(.width(1)) adder_1 (.a(A), .b(multiplexer_1_out), .out(adder_1_out), .cin(Cin), .cout(Cout));
  Multiplexer #(.select(2), .enable("false")) multiplexer_2 (
    .in0(and_1_out), .in1(or_1_out), .in2(xor_1_out), .in3(adder_1_out), .out(out_6), .sel(Operation));
endmodule
