// Logisim project kerucpu.circ as structural Verilog
module k_adder (
  input  Cin,
  input  A,
  input  B,
  output Cout,
  output Sum
);

  wire and_1_out, and_2_out, xor_2_out;

  and and_1 (and_1_out, A, B);
  or or_1 (Cout, and_1_out, and_2_out);
  and and_2 (and_2_out, Cin, xor_2_out);
  xor xor_1 (Sum, Cin, xor_2_out);
  xor xor_2 (xor_2_out, A, B);

  // Notes on the sheet:
  //   Kerunix full adder
endmodule

module k_4bit_adder (
  input  Cin,
  input  A0,
  input  A1,
  input  A2,
  input  A3,
  input  B0,
  input  B1,
  input  B2,
  input  B3,
  output S0,
  output S1,
  output S2,
  output S3,
  output Cout
);

  wire k_adder_1_cout, k_adder_2_cout, k_adder_3_cout;

  k_adder k_adder_1 (.Cout(k_adder_1_cout), .Sum(S0), .Cin(Cin), .A(A0), .B(B0));
  k_adder k_adder_2 (.Cout(k_adder_2_cout), .Sum(S1), .Cin(k_adder_1_cout), .A(A1), .B(B1));
  k_adder k_adder_3 (.Cout(k_adder_3_cout), .Sum(S2), .Cin(k_adder_2_cout), .A(A2), .B(B2));
  k_adder k_adder_4 (.Cout(Cout), .Sum(S3), .Cin(k_adder_3_cout), .A(A3), .B(B3));
endmodule
